# Fritzing sketch Car (saved by Fritzing 0.9.3b)
breadboards: 1

parts:
  Raspberry_Pi_1 = Raspberry Pi 3 [part_number=RPI-3-V1.2]
  VCC1 = Battery block 9V
  IC1 = L293D [package=THT]
  J1 = Basic Servo
  M2 = DC Motor
  M1 = DC Motor

nets:
  N1: Raspberry_Pi_1.GPIO21, IC1.Enable_1
  N2: Raspberry_Pi_1.GPIO20, IC1.In_1
  N3: Raspberry_Pi_1.GPIO16, IC1.In_2
  N4: Raspberry_Pi_1.GPIO18, J1.pulse
  GND: Raspberry_Pi_1.GND, VCC1.-, IC1.0V, J1.gnd, M1.pin_1
  5V: Raspberry_Pi_1.5V, IC1.+V, J1.vcc
  N5: VCC1.+, IC1.+Vmotor, M2.pin_1
  N6: IC1.Out_1_(_Controlled_by_Enable_1_), M1.pin_2
  N7: IC1.Out_2_(_Controlled_by_Enable_1_), M2.pin_2
